# Fritzing sketch wemos_pcb (saved by Fritzing 0.9.2b)
circuit board: 4.4cm x 5.8cm

parts:
  WeMos_D1_Mini1 = WeMos D1 Mini
  FET = Basic FET N-Channel [package="TO220 [THT]"]
  R1 = Resistor [tolerance=±5% resistance=220 package=THT]
  Card_Reader = female pin header, 6 pins [form="♀ (female)"]
  Emrg_Rel = female pin header, 2 pins [form="♀ (female)"]
  Latch = female pin header, 4 pins [form="♀ (female)"]
  Power = female alternating pin header, 3 pins [form="♀ (female)"]

nets:
  N1: WeMos_D1_Mini1.3V3, Power.pin3
  N2: WeMos_D1_Mini1.D0, Card_Reader.pin3
  N3: WeMos_D1_Mini1.D3, Latch.pin4
  N4: WeMos_D1_Mini1.D4, Emrg_Rel.pin2
  N5: WeMos_D1_Mini1.D5, Card_Reader.pin4
  N6: WeMos_D1_Mini1.D6, Card_Reader.pin5
  N7: WeMos_D1_Mini1.D7, Card_Reader.pin6
  N8: WeMos_D1_Mini1.D8, R1.Pin_0
  N9: WeMos_D1_Mini1.G, FET.source, Card_Reader.pin2, Emrg_Rel.pin1, Latch.pin3, Power.pin2
  N10: FET.gate, R1.Pin_1
  N11: FET.drain, Latch.pin2
  N12: Card_Reader.pin1, Latch.pin1, Power.pin1

notes:
  +12v    Gnd   +3.3v
  Coil+
  Coil-
  Sense-
  Sense+
  +12v
  Gnd
  Beep
  LED
  D0
  D1
  Sense  Gnd  Coil- Coil+
  +3v3  Gnd  +12v
  D1   D0  Beep  LED  Gnd +12v
  G   D   S
  DoorLock v2.0
  Sense Gnd
