# Fritzing sketch wemos_breadboard (saved by Fritzing 0.9.2b)
stripboards: 1

parts:
  WeMos_D1_Mini1 = WeMos D1 Mini
  Q1 = Basic FET N-Channel [package="TO220 [THT]"]
  R1 = Resistor [tolerance=±5% resistance=220 package=THT]
  R2 = Resistor [tolerance=±5% resistance=220 package=THT]
  J1 = female pin header, 8 pins [form="♀ (female)"]
  J2 = female pin header, 3 pins [form="♀ (female)"]

nets:
  N1: WeMos_D1_Mini1.3V3, J1.pin1, J2.pin2
  N2: WeMos_D1_Mini1.D0, R1.Pin_0
  N3: WeMos_D1_Mini1.D1, J1.pin2
  N4: WeMos_D1_Mini1.D2, J1.pin4
  N5: WeMos_D1_Mini1.D5, J1.pin7
  N6: WeMos_D1_Mini1.D6, J1.pin5
  N7: WeMos_D1_Mini1.D7, J1.pin6
  N8: WeMos_D1_Mini1.D8, J1.pin8
  N9: WeMos_D1_Mini1.G, Q1.source, R2.Pin_0, J1.pin3, J2.pin3
  N10: Q1.gate, R1.Pin_1, R2.Pin_1
  N11: Q1.drain, J2.pin1
